# Fritzing sketch Alarm_Clock_MAX7219_Schematic (saved by Fritzing 0.7.12b)
breadboards: 2

parts:
  Arduino2 = Arduino
  R3 = Resistor [tolerance=±5% resistance=220 package=THT]
  R4 = Resistor [tolerance=±5% resistance=220 package=THT]
  R5 = Resistor [tolerance=±5% resistance=220 package=THT]
  Part1 = Real Time Clock Module - DS1307 RTC Breakout Board
  J1 = Piezo Speaker
  IC3 = IC, DIP package, 24 pins [chip_label=MAX2719]
  J7 = female pin header, 6 pins [form="♀ (female)"]
  J8 = female pin header, 6 pins [form="♀ (female)"]
  R7 = Resistor [tolerance=±5% resistance=220 package=THT]
  J9 = female pin header, 5 pins [form="♀ (female)"]
  C5 = Electrolytic Capacitor [capacitance=1µF package="100 mil [THT, electrolytic]"]
  C6 = Ceramic Capacitor [capacitance=100nF package="100 mil [THT, multilayer]"]
  ENCODER1 = Rotary Encoder with Knob

nets:
  N1: Arduino2.D11, R3.Pin_0, ENCODER1.no_name_yet#3
  N2: Arduino2.D10, R4.Pin_0, ENCODER1.no_name_yet#1
  N3: Arduino2.D9, J1.pin2
  N4: Arduino2.D8, R5.Pin_1, ENCODER1.no_name_yet#5
  N5: Arduino2.D5, IC3.pin12, J9.pin3
  N6: Arduino2.D4, IC3.pin13, J9.pin2
  N7: Arduino2.D3, IC3.pin1, J9.pin1
  N8: Arduino2.A4, Part1.SDA
  N9: Arduino2.A5, Part1.SCL
  N10: R3.Pin_1, R4.Pin_1, Part1.5V, IC3.pin19, R7.Pin_0, J9.pin5, C5.+, C6.1, ENCODER1.no_name_yet#4
  N11: R5.Pin_0, Part1.GND, J1.pin1, IC3.pin4, J9.pin4, C5.-, C6.0, ENCODER1.no_name_yet#2
  N12: IC3.pin2, J7.pin6
  N13: IC3.pin6, J8.pin4
  N14: IC3.pin7, J8.pin1
  N15: IC3.pin11, J8.pin5
  N16: IC3.pin14, J8.pin2
  N17: IC3.pin15, J8.pin3
  N18: IC3.pin16, J8.pin6
  N19: IC3.pin17, J7.pin5
  N20: IC3.pin18, R7.Pin_1
  N21: IC3.pin20, J7.pin4
  N22: IC3.pin21, J7.pin1
  N23: IC3.pin22, J7.pin3
  N24: IC3.pin23, J7.pin2

custom parts:
  Rotary Encoder with Knob: Rotary Encoder with 1/4" Shaft and Knob
